# Fritzing sketch fritzing_diagram (saved by Fritzing 0.9.2b)
breadboards: 1

parts:
  Part1 = Intel Edison Arduinobreakout
  S1 = Pushbutton [package="[THT]"]
  S2 = Pushbutton [package="[THT]"]
  S3 = Pushbutton [package="[THT]"]
  R1 = Resistor [tolerance=±5% resistance=10k package=THT]
  R4 = Resistor [tolerance=±5% resistance=10k package=THT]
  R5 = Resistor [tolerance=±5% resistance=10k package=THT]

nets:
  N1: Part1.GND, S1.Pin_1, S1.Pin_2, S2.Pin_1, S2.Pin_2, S3.Pin_1, S3.Pin_2
  N2: Part1.D3_PWM, S1.Pin_3, S1.Pin_4, R1.Pin_0
  N3: Part1.D4, S2.Pin_3, S2.Pin_4, R4.Pin_0
  N4: Part1.D5_PWM, S3.Pin_3, S3.Pin_4, R5.Pin_0
  N5: Part1.5V, R1.Pin_1, R4.Pin_1, R5.Pin_1
